# Fritzing sketch Counter (saved by Fritzing 0.9.10b)

parts:
  Amica_NodeMCU_DevKit_1_1 = Amica NodeMCU DevKit 1.0
  J1 = Camdenboss CTB0158-3 [part_number="RH Electronics Geiger Counter DIY Kit 3.0" package=THT]

nets:
  N1: Amica_NodeMCU_DevKit_1_1.pin2, Amica_NodeMCU_DevKit_1_1.pin_29, J1.pin3
  N2: Amica_NodeMCU_DevKit_1_1.pin_13, J1.pin2
  N3: Amica_NodeMCU_DevKit_1_1.pin_30, J1.pin1

notes:
  5V
  INT
  GND
  Geiger Counter for radmon.org, Can be powered by either the NodeMCU USB connector or by an external 5V source connected to the Geiger counter, 1
  Geiger Counter

custom parts:
  Amica NodeMCU DevKit 1.0: Amica NodeMCU DEVKIT 1.0 Development Kit based on ESP8266 ESP-12E, integating GPIO, PWM, IIC, 1-Wire and ADC all in one board.
